# Fritzing sketch Arduino-Oil-Level-Logger (saved by Fritzing 0.9.2b)
breadboards: 1

parts:
  U1 = 3.5mm Audio Jack [package=audio-jack-3.5mm-smd]
  JP1 = RCA [package=rca_lock]
  Part1 = Arduino Uno (Rev3)
  R1 = Resistor [tolerance=±5% resistance=4.7k package="0402 [SMD]"]

nets:
  N1: U1.RIGHT, JP1.SHELL, Part1.GND
  N2: U1.SLEEVE, Part1.5V, R1.Pin_1
  N3: U1.LEFT, Part1.D8
  N4: JP1.SWITCH, Part1.D2, R1.Pin_0
