# Fritzing sketch Arduino-Ultrasonic-sensor-subsystem (saved by Fritzing 0.9.2b)
breadboards: 1

parts:
  SONAR1 = Maxbotix MaxSonar Ultrasonic Sensor [part_number=LV-EZ1]
  U2 = AUDIO-JACK2 [part_number="3.5mm AV connector" package=audio-jack-3.5mm-smd]

nets:
  N1: SONAR1.GND, U2.RING
  N2: SONAR1.+5V, U2.RSH
  N3: SONAR1.PW, U2.TSH

custom parts:
  Maxbotix MaxSonar Ultrasonic Sensor: Maxbotix MaxSonar Ultrasonic Sensor LV-EZ0, LV-EZ1, LV-EZ2, LV-EZ3, LV-EZ4
